// Logisim project contador_basico.circ as structural Verilog: 1 circuit, main circuit main
module main (
);

  wire CLK_out, FF2_p1, FF3_p1, FF3_p3;

  Clock CLK (.out(CLK_out));
  Button RESET ();  // open: out
  J_K_Flip_Flop FF1 (.Q(CLK_out));  // open: J, clk, K, Qn, preset, en, reset
  // J_K_Flip_Flop FF2: pin names not known; wires that end beside it: FF2_p1, CLK_out
  // J_K_Flip_Flop FF3: pin names not known; wires that end beside it: FF3_p1, CLK_out, FF3_p3
  LED Q1 (.in(FF2_p1));
  LED Q2 (.in(FF3_p1));
  LED Q3 (.in(FF3_p3));
endmodule
