// Logisim project reloj_completo.circ as structural Verilog: 1 circuit, main circuit main
module main (
);

  wire CLK_out, Detect_HH_23_p8, HH_FF1_p1, HH_FF1_p2, HH_FF2_p3, HH_FF2_p4, HH_FF3_p4, HH_FF3_p5, HH_FF4_p4,
       HH_FF4_p5, MM_FF0_p2, MM_FF1_p2, MM_FF2_p3, MM_FF2_p4, MM_FF3_p4, MM_FF3_p5, MM_FF4_p4, MM_FF4_p5,
       MM_FF5_p4, MM_FF5_p5, Reset_Global_p4, SS_FF1_p1, SS_FF1_p2, SS_FF2_p3, SS_FF2_p4, SS_FF3_p4,
       SS_FF3_p5, SS_FF4_p4, SS_FF4_p5, SS_FF5_p4, SS_FF5_p5;
  wire [3:0] HH_FF1_p3, MM_FF1_p3, SS_FF1_p3;

  Clock CLK (.out(CLK_out));
  Button RESET ();  // open: out
  J_K_Flip_Flop SS_FF0 (.Q(CLK_out));  // open: J, clk, K, Qn, preset, en, reset
  // J_K_Flip_Flop MM_FF0: pin names not known; wires that end beside it: CLK_out, MM_FF0_p2
  J_K_Flip_Flop HH_FF0 (.Q(CLK_out));  // open: J, clk, K, Qn, preset, en, reset
  // J_K_Flip_Flop SS_FF1: pin names not known; wires that end beside it: SS_FF1_p1, SS_FF1_p2, SS_FF1_p3
  // J_K_Flip_Flop SS_FF2: pin names not known; wires that end beside it: SS_FF1_p1, SS_FF1_p3, SS_FF2_p3, SS_FF2_p4, SS_FF2_p4
  // J_K_Flip_Flop MM_FF1: pin names not known; wires that end beside it: MM_FF0_p2, MM_FF1_p2, MM_FF1_p3
  // J_K_Flip_Flop MM_FF2: pin names not known; wires that end beside it: MM_FF0_p2, MM_FF1_p3, MM_FF2_p3, MM_FF2_p4, MM_FF2_p4
  // J_K_Flip_Flop HH_FF1: pin names not known; wires that end beside it: HH_FF1_p1, HH_FF1_p2, HH_FF1_p3
  // J_K_Flip_Flop HH_FF2: pin names not known; wires that end beside it: HH_FF1_p1, HH_FF1_p3, HH_FF2_p3, HH_FF2_p4, HH_FF2_p4
  // J_K_Flip_Flop SS_FF3: pin names not known; wires that end beside it: SS_FF1_p3, SS_FF2_p4, SS_FF2_p4, SS_FF3_p4, SS_FF3_p5, SS_FF3_p5
  // J_K_Flip_Flop MM_FF3: pin names not known; wires that end beside it: MM_FF1_p3, MM_FF2_p4, MM_FF2_p4, MM_FF3_p4, MM_FF3_p5, MM_FF3_p5
  // J_K_Flip_Flop HH_FF3: pin names not known; wires that end beside it: HH_FF1_p3, HH_FF2_p4, HH_FF2_p4, HH_FF3_p4, HH_FF3_p5, HH_FF3_p5
  // J_K_Flip_Flop SS_FF4: pin names not known; wires that end beside it: SS_FF2_p4, SS_FF3_p5, SS_FF3_p5, SS_FF4_p4, SS_FF4_p5, SS_FF4_p5
  // J_K_Flip_Flop SS_FF5: pin names not known; wires that end beside it: SS_FF3_p5, SS_FF4_p5, SS_FF4_p5, SS_FF5_p4, SS_FF5_p5
  // J_K_Flip_Flop MM_FF4: pin names not known; wires that end beside it: MM_FF2_p4, MM_FF3_p5, MM_FF3_p5, MM_FF4_p4, MM_FF4_p5, MM_FF4_p5
  // J_K_Flip_Flop MM_FF5: pin names not known; wires that end beside it: MM_FF3_p5, MM_FF4_p5, MM_FF4_p5, MM_FF5_p4, MM_FF5_p5
  // J_K_Flip_Flop HH_FF4: pin names not known; wires that end beside it: HH_FF2_p4, HH_FF3_p5, HH_FF3_p5, HH_FF4_p4, HH_FF4_p5
  // AND_Gate Detect_SS_59: pin names not known; wires that end beside it: SS_FF5_p5, SS_FF5_p5, SS_FF5_p4, SS_FF4_p4, SS_FF3_p4, SS_FF2_p3
  // AND_Gate Detect_MM_59: pin names not known; wires that end beside it: MM_FF5_p5, SS_FF2_p3, SS_FF1_p2, MM_FF5_p5, MM_FF5_p4, MM_FF4_p4, MM_FF3_p4, MM_FF2_p3, MM_FF1_p2
  // AND_Gate Detect_HH_23: pin names not known; wires that end beside it: HH_FF4_p5, HH_FF4_p4, HH_FF3_p4, HH_FF2_p3, HH_FF1_p2, MM_FF2_p3, MM_FF1_p2, Detect_HH_23_p8
  // Label #(.text("HH")) label_1: pin names not known
  // AND_Gate Carry_SS_MM: pin names not known; wires that end beside it: SS_FF5_p5, SS_FF2_p3, MM_FF5_p5
  // Label #(.text("MM")) label_2: pin names not known
  // AND_Gate Carry_MM_HH: pin names not known; wires that end beside it: MM_FF5_p5, MM_FF2_p3, MM_FF1_p2, Detect_HH_23_p8
  // Label #(.text("SS")) label_3: pin names not known
  // AND_Gate Reset_Global: pin names not known; wires that end beside it: CLK_out, CLK_out, Detect_HH_23_p8, Reset_Global_p4
  // Hex_Digit_Display Horas_Decena: pin names not known; wires that end beside it: SS_FF1_p1
  // Hex_Digit_Display Minutos_Decena: pin names not known; wires that end beside it: Reset_Global_p4, MM_FF0_p2
  // Hex_Digit_Display Segundos_Decena: pin names not known; wires that end beside it: HH_FF1_p1
  Hex_Digit_Display Horas_Unidad (.value(SS_FF1_p3));  // open: dp
  Hex_Digit_Display Minutos_Unidad (.value(MM_FF1_p3));  // open: dp
  Hex_Digit_Display Segundos_Unidad (.value(HH_FF1_p3));  // open: dp

  // Notes on the sheet:
  //   HH:MM:SS
endmodule
