// Logisim project reloj_digital.circ as structural Verilog: 3 circuits, main circuit main
module main (
);

  wire clock_1_out, Reset_out;

  Clock clock_1 (.out(clock_1_out));
  Button Reset (.out(Reset_out));
  // contador_mod60_main Contador_Segundos: pin names not known; wires that end beside it: clock_1_out
  // contador_mod60_main Contador_Minutos: pin names not known
  // contador_mod24_main Contador_Horas: pin names not known
  // AND_Gate Carry_a_Minutos is placed but not wired
  // AND_Gate Carry_a_Horas is placed but not wired
  // AND_Gate Reset_Global has open pins: out=Reset_out
  // Label #(.text("Horas")) label_1: pin names not known
  // Label #(.text("Minutos")) label_2: pin names not known
  // Label #(.text("Segundos")) label_3: pin names not known
  Hex_Digit_Display hex_digit_display_1 ();  // open: value, dp
  Hex_Digit_Display hex_digit_display_2 ();  // open: value, dp
  Hex_Digit_Display hex_digit_display_3 ();  // open: value, dp
endmodule

module contador_mod60 (
);

  J_K_Flip_Flop FF0__LSB ();  // open: J, clk, K, Q, Qn, preset, en, reset
  J_K_Flip_Flop FF1 ();  // open: J, clk, K, Q, Qn, preset, en, reset
  J_K_Flip_Flop FF2 ();  // open: J, clk, K, Q, Qn, preset, en, reset
  J_K_Flip_Flop FF3 ();  // open: J, clk, K, Q, Qn, preset, en, reset
  J_K_Flip_Flop FF4 ();  // open: J, clk, K, Q, Qn, preset, en, reset
  J_K_Flip_Flop FF5__MSB ();  // open: J, clk, K, Q, Qn, preset, en, reset
  // AND_Gate Detectar_59 is placed but not wired
  // Output Carry: pin names not known
endmodule

module contador_mod24 (
);

  wire undriven;

  J_K_Flip_Flop FF0__LSB ();  // open: J, clk, K, Q, Qn, preset, en, reset
  J_K_Flip_Flop FF1 ();  // open: J, clk, K, Q, Qn, preset, en, reset
  J_K_Flip_Flop FF2 ();  // open: J, clk, K, Q, Qn, preset, en, reset
  J_K_Flip_Flop FF3 ();  // open: J, clk, K, Q, Qn, preset, en, reset
  J_K_Flip_Flop FF4__MSB ();  // open: J, clk, K, Q, Qn, preset, en, reset
  // NOT_Gate NOT_FF2 has open pins: in=undriven, out=open
  // AND_Gate Detectar_23 has open pins: in4=undriven, out=open
  // Output Carry: pin names not known
endmodule
