// Logisim project reloj_simple.circ as structural Verilog: 1 circuit, main circuit main
module main (
);

  wire clock_1_out, HH1_p1, HH2_p2, HH2_p3, HH3_p4, MM1_p1, MM2_p2, MM2_p3, MM3_p4, MM4_p4, SS0_p1, SS1_p1,
       SS2_p2, SS2_p3, SS3_p4, SS4_p4;

  Clock clock_1 (.out(clock_1_out));
  Button Reset ();  // open: out
  // J_K_Flip_Flop SS0: pin names not known; wires that end beside it: SS0_p1
  // J_K_Flip_Flop MM0: pin names not known; wires that end beside it: SS0_p1
  // J_K_Flip_Flop HH0: pin names not known; wires that end beside it: clock_1_out, SS0_p1
  // J_K_Flip_Flop SS1: pin names not known; wires that end beside it: SS1_p1
  // J_K_Flip_Flop MM1: pin names not known; wires that end beside it: MM1_p1
  // J_K_Flip_Flop HH1: pin names not known; wires that end beside it: HH1_p1
  // J_K_Flip_Flop SS2: pin names not known; wires that end beside it: SS1_p1, SS2_p2, SS2_p3
  // J_K_Flip_Flop SS3: pin names not known; wires that end beside it: SS2_p2, SS2_p3, SS2_p3, SS3_p4
  // J_K_Flip_Flop MM2: pin names not known; wires that end beside it: MM1_p1, MM2_p2, MM2_p3
  // J_K_Flip_Flop MM3: pin names not known; wires that end beside it: MM2_p2, MM2_p3, MM2_p3, MM3_p4
  // J_K_Flip_Flop HH2: pin names not known; wires that end beside it: HH1_p1, HH2_p2, HH2_p3
  // J_K_Flip_Flop HH3: pin names not known; wires that end beside it: HH2_p2, HH2_p3, HH2_p3, HH3_p4
  // J_K_Flip_Flop SS4: pin names not known; wires that end beside it: SS2_p3, SS3_p4, SS3_p4, SS4_p4
  // J_K_Flip_Flop MM4: pin names not known; wires that end beside it: MM2_p3, MM3_p4, MM3_p4, MM4_p4
  // J_K_Flip_Flop HH4: pin names not known; wires that end beside it: HH2_p3, HH3_p4, HH3_p4
  // J_K_Flip_Flop SS5: pin names not known; wires that end beside it: SS3_p4, SS4_p4, SS4_p4
  // J_K_Flip_Flop MM5: pin names not known; wires that end beside it: MM3_p4, MM4_p4, MM4_p4
  // _7_Segment_Display 7_segment_display_1: pin names not known; wires that end beside it: SS1_p1
  // _7_Segment_Display 7_segment_display_2: pin names not known; wires that end beside it: MM1_p1
  // _7_Segment_Display 7_segment_display_3: pin names not known; wires that end beside it: HH1_p1
  _7_Segment_Display u_7_segment_display_4 (.g(SS2_p2));  // open: f, a, b, e, d, c, dp
  _7_Segment_Display u_7_segment_display_5 (.g(MM2_p2));  // open: f, a, b, e, d, c, dp
  _7_Segment_Display u_7_segment_display_6 (.g(HH2_p2));  // open: f, a, b, e, d, c, dp

  // Notes on the sheet:
  //   RELOJ DIGITAL 24 HORAS
  //   Horas
  //   Minutos
  //   Segundos
  //   :
  //   :
endmodule
